# Fritzing sketch Esquematico Node Atuador (saved by Fritzing 0.9.2b)
breadboards: 1

parts:
  U1 = ESP8266 WiFi Module [part_number=ESP8266]
  Source_5V = DC Power [voltage=5]
  Out_3_3V = V_REG_LD1117VXX [package=78xxl]
  U2 = RELAY [package=relay-jzc]
  Q1 = NPN-Transistor [package="TO92 [THT]"]
  R1 = Resistor [tolerance=±5% resistance=1k package="0603 [SMD]"]
  Load = Screw terminal - 2 pins [package=THT]

nets:
  N1: U1.VCC, Out_3_3V.OUT
  GND: U1.GND, Source_5V.V-, Out_3_3V.GND, Q1.E
  N2: U1.GPIO_4, R1.Pin_0
  N3: Source_5V.V+, Out_3_3V.IN, U2.COIL1
  N4: U2.COIL2, Q1.C
  N5: U2.NO, Load.pin2
  N6: U2.MAIN, Load.pin1
  N7: Q1.B, R1.Pin_1
