# Fritzing sketch Esquematico Node Coleta Dados (saved by Fritzing 0.9.2b)
breadboards: 1

parts:
  U1 = ESP8266 WiFi Module [part_number=ESP8266]
  Source_5V = DC Power [voltage=5]
  Out_3_3V = V_REG_LD1117VXX [package=78xxl]
  DHT22 = DHT22 Humidity and Temperature Sensor
  BMP180 = Adafruit BMP180
  Part1 = FC-28 Soil Hygrometer Module
  R1 = Resistor [tolerance=±5% resistance=10k package="0402 [SMD]"]
  S2 = SWITCH-MOMENTARY-2 [package=tactile-switch-1101ne]
  R2 = Resistor [tolerance=±5% resistance=10k package="0402 [SMD]"]
  LED1 = LED - 5mm [color="Red (633nm)" package="5 mm [THT]"]
  R3 = Resistor [tolerance=±5% resistance=100 package=THT]

nets:
  VCC: U1.VCC, Out_3_3V.OUT, DHT22.VDD, BMP180.+3V3, R1.Pin_0, R2.Pin_0, R3.Pin_0
  N1: U1.GPIO_0, BMP180.SDA
  N2: U1.GPIO_2, BMP180.SCL
  GND: U1.GND, Source_5V.V-, Out_3_3V.GND, DHT22.GND, BMP180.GND, Part1.GND, S2.2
  N3: U1.GPIO_4, LED1.cathode
  N4: U1.GPIO_5, DHT22.DATA, R1.Pin_1
  N5: U1.ADC_0, Part1.AO
  N6: U1.GPIO_12, S2.1
  N7: Source_5V.V+, Out_3_3V.IN, Part1.VCC
  N8: LED1.anode, R3.Pin_1

custom parts:
  Adafruit BMP180: This precision sensor from Bosch is the best low-cost sensing solution for measuring barometric pressure and temperature. Because pressure changes with altitude you can also use it as an altimeter! The sensor is soldered onto a PCB with a 3.3V regulator, I2C level shifter and pull-up resistors on the I2C pins. The BMP180 is the next-generation of sensors from Bosch, and replaces the BMP085.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
  FC-28 Soil Hygrometer Module: The FC-28 is a soil hygrometer module that uses the Texas Instruments LM393 comparator chip to provide an analog measurement of soil humidity. The digital output is high when soil moisture is over a certain threshold, as determined by adjusting the potentiometer.
